# Fritzing sketch Fritzing Sketch (saved by Fritzing 0.9.3b)
breadboards: 1

parts:
  Part1 = Arduino Uno (Rev3)
  S1 = Momentary Switch [package=ksa_sealed_tac_switch]
  S2 = Momentary Switch [package=ksa_sealed_tac_switch]
  S3 = Momentary Switch [package=ksa_sealed_tac_switch]
  J1 = Basic Servo

nets:
  N1: Part1.D10_PWM/SS, J1.pulse
  N2: Part1.D4, S2.1
  N3: Part1.D5_PWM, S1.1
  N4: Part1.D6_PWM, S3.3
  5V: Part1.5V, J1.vcc
  GND: Part1.GND, S1.3, S2.3, S3.1, J1.gnd
